# Fritzing sketch wiering_wateringmachine (saved by Fritzing 0.9.3b)
breadboards: 1

parts:
  Bauteil1 = Arduino Nano (Rev3.0)
  Q1 = NPN-Transistor [package="TO92 [THT]"]
  Q2 = NPN-Transistor [package="TO92 [THT]"]
  Q3 = Basic FET P-Channel [package="TO220 [THT]"]
  S1 = Pushbutton [package="[THT]"]
  RE1 = Rotary Encoder [package=THT]
  LCD1 = LCD screen
  9V = Power plug
  R1 = Resistor [tolerance=±5% resistance=1k package=THT]
  R2 = Resistor [tolerance=±5% resistance=1k package=THT]
  R3 = Resistor [tolerance=±5% resistance=1k package=THT]
  J1 = Piezo Speaker
  Bauteil2 = Soil Moisture Sensor
  Pump = Solenoid

nets:
  GND: Bauteil1.GND, Q1.E, Q3.source, 9V.GND, R3.Pin_0, J1.pin1, Bauteil2.GND
  N1: Bauteil1.D2, LCD1.DB7
  N2: Bauteil1.D3, LCD1.DB6
  N3: Bauteil1.D4, LCD1.DB5
  N4: Bauteil1.D5, LCD1.DB4
  N5: Bauteil1.D6, Q3.gate
  N6: Bauteil1.D7, J1.pin2
  N7: Bauteil1.D8, S1.Pin_3, S1.Pin_4, R3.Pin_1
  N8: Bauteil1.D9, R1.Pin_0, R2.Pin_1
  N9: Bauteil1.D11/MOSI, LCD1.E
  N10: Bauteil1.D12/MISO, LCD1.RS
  5V: Bauteil1.5V, Q2.E, S1.Pin_1, S1.Pin_2, Bauteil2.VCC
  N11: Bauteil1.A0, Bauteil2.SIG
  N12: Q1.B, R1.Pin_1
  N13: Q1.C, RE1.EncoderPinB, LCD1.VSS, LCD1.R/W, LCD1.LED-
  N14: Q2.B, R2.Pin_0
  N15: Q2.C, RE1.EncoderPinA, LCD1.VDD, LCD1.LED+
  N16: Q3.drain, Pump.pin1
  N17: RE1.EncoderPinC, LCD1.V0
  N18: 9V.VCC, Pump.pin2
